# Fritzing sketch circuit-design (saved by Fritzing 0.9.3b)
breadboards: 1

parts:
  Part1 = Arduino Nano (Rev3.0)
  MQ-3_Ethanol/Alcohol_D/A_Sensor = MQ-3 breakout
  LED1 = LED - 3mm [color="Red (633nm)" package="3 mm [THT]"]

nets:
  GND: Part1.GND, MQ-3_Ethanol/Alcohol_D/A_Sensor.GND, LED1.cathode
  N1: Part1.D8, MQ-3_Ethanol/Alcohol_D/A_Sensor.DO
  5V: Part1.5V, MQ-3_Ethanol/Alcohol_D/A_Sensor.VCC
  N2: Part1.A0, MQ-3_Ethanol/Alcohol_D/A_Sensor.AO
  N3: Part1.D13/SCK, LED1.anode

custom parts:
  MQ-3 breakout: Alcohol sensor is capable of detecting alcohol (ethanol) particles on itself and gives the information in digital form back to us to manipulate with it. SKU:101251 • Voltage: 5V DC • Power: max 750mW • Measurement range: 0.04-4mg/L
